# Fritzing sketch Untitled_Sketch (saved by Fritzing 0.9.3b)

parts:
  Composant1 = Arduino Uno (Rev3)  # not connected
  Composant2 = Base Shield V2
  Grove_LED_Red1 = Grove LED Red
  Grove_LED_Red2 = Grove LED Red
  Grove_LED_Red3 = Grove LED Red
  Grove1 = Grove Button

nets:
  N1: Composant2.pin_96, Grove1.GND
  N2: Composant2.pin_97, Grove1.VCC
  N3: Composant2.pin_98, Grove1.NC
  N4: Composant2.pin_99, Grove1.SIG
  N5: Composant2.pin_100, Grove_LED_Red1.GND
  N6: Composant2.pin_101, Grove_LED_Red1.NC2
  N7: Composant2.pin_102, Grove_LED_Red1.NC1
  N8: Composant2.pin_103, Grove_LED_Red1.SIG
  N9: Composant2.pin_104, Grove_LED_Red2.GND
  N10: Composant2.pin_105, Grove_LED_Red2.NC2
  N11: Composant2.pin_106, Grove_LED_Red2.NC1
  N12: Composant2.pin_107, Grove_LED_Red2.SIG
  N13: Composant2.pin_108, Grove_LED_Red3.GND
  N14: Composant2.pin_109, Grove_LED_Red3.NC2
  N15: Composant2.pin_110, Grove_LED_Red3.NC1
  N16: Composant2.pin_111, Grove_LED_Red3.SIG

custom parts:
  Grove LED Red: LED red, Grove connector.
